// Logisim project projet2.circ as structural Verilog
module MicroIndirect (
);

  wire and_1_out, and_2_out, and_3_out, and_4_out, and_5_out, and_6_out, and_7_out, c_alu_16_bits_1_negative,
       c_alu_16_bits_1_zero, c_cycle_1_etat_1, c_cycle_1_etat_2, c_cycle_1_etat_3, c_cycle_1_etat_4,
       clock_1_out, not_1_out, not_2_out, not_3_out, or_1_out;
  wire [4:0] Sauts;
  wire [15:0] c_alu_16_bits_1_output, c_compteur_16bits_1_output, c_mux_1_output, c_mux_2_output,
       c_mux_3_output, Registre_A_q, Registre_B_q, Registre_C_q, rom_2_data;
  wire [31:0] register_1_q, rom_1_data;

  Clock clock_1 (.out(clock_1_out));
  c_Compteur_16bits c_compteur_16bits_1 (
    .Output(c_compteur_16bits_1_output), .Input(c_mux_2_output), .Reset(or_1_out), .Control(c_cycle_1_etat_4));
  // Probe on c_compteur_16bits_1_output
  c_Cycle c_cycle_1 (
    .\Entrée_Horloge (clock_1_out), .Etat_1(c_cycle_1_etat_1), .Etat_2(c_cycle_1_etat_2),
    .Etat_3(c_cycle_1_etat_3), .Etat_4(c_cycle_1_etat_4));
  and and_1 (and_1_out, c_alu_16_bits_1_zero, Sauts[0]);
  and and_2 (and_2_out, not_1_out, Sauts[1]);
  and and_3 (and_3_out, c_alu_16_bits_1_negative, Sauts[2]);
  or or_1 (or_1_out, and_1_out, and_2_out, and_3_out, and_4_out, Sauts[4]);
  and and_4 (and_4_out, not_2_out, Sauts[3]);
  Register #(.width(32), .trigger("high")) register_1 (
    .D(rom_1_data), .Q({register_1_q[31:21], Sauts, register_1_q[15:0]}), .clk(c_cycle_1_etat_1));  // open: en, clr
  ROM #(.addrWidth(16), .dataWidth(32)) rom_1 (.addr(c_compteur_16bits_1_output), .data(rom_1_data));  // open: sel
  not not_1 (not_1_out, c_alu_16_bits_1_zero);
  not not_2 (not_2_out, c_alu_16_bits_1_negative);
  // Probe on c_mux_1_output
  c_ALU_16_bits c_alu_16_bits_1 (
    .Input_1(c_mux_1_output), .Input_0(c_mux_2_output), .Output(c_alu_16_bits_1_output),
    .Negative(c_alu_16_bits_1_negative), .Zero(c_alu_16_bits_1_zero), .C3(register_1_q[28]),
    .C2(register_1_q[27]), .C1(register_1_q[26]), .C0(register_1_q[25]), .Enable(c_cycle_1_etat_2));  // open: Carry
  // Probe on c_alu_16_bits_1_output
  c_MUX c_mux_1 (
    .Output(c_mux_1_output), .Input_0(c_alu_16_bits_1_output), .Input_1(c_mux_3_output), .Control(not_3_out));
  // Probe on c_mux_1_output
  // Probe on {register_1_q[31:21], Sauts, register_1_q[15:0]}
  // Probe on c_mux_2_output
  not not_3 (not_3_out, register_1_q[30]);
  ROM #(.addrWidth(16), .dataWidth(16)) rom_2 (.addr(c_mux_1_output), .data(rom_2_data));  // open: sel
  // Probe on c_mux_2_output
  c_MUX c_mux_2 (
    .Output(c_mux_2_output), .Input_0(register_1_q[15:0]), .Input_1(Registre_A_q), .Control(register_1_q[29]));
  Register #(.width(16)) Registre_A (.D(c_alu_16_bits_1_output), .Q(Registre_A_q), .clk(and_5_out));  // open: en, clr
  Register #(.width(16)) Registre_B (.D(c_alu_16_bits_1_output), .Q(Registre_B_q), .clk(and_6_out));  // open: en, clr
  c_MUX c_mux_3 (.Output(c_mux_3_output), .Input_0(Registre_B_q), .Input_1(Registre_C_q), .Control(register_1_q[22]));
  Register #(.width(16)) Registre_C (.D(rom_2_data), .Q(Registre_C_q), .clk(and_7_out));  // open: en, clr
  // Probe on rom_2_data
  // Probe on register_1_q[15:0]
  // Probe on Registre_A_q
  and and_5 (and_5_out, register_1_q[24], c_cycle_1_etat_3);
  and and_6 (and_6_out, register_1_q[23], c_cycle_1_etat_3);
  and and_7 (and_7_out, register_1_q[21], c_cycle_1_etat_3);
  // Probe on {register_1_q[31:21], Sauts}
  Table_ALU table_alu_1 ();

  // Notes on the sheet:
  //   1.Lecture Mémoire
  //   Mémoire Programme
  //   JMP
  //   4.Incrémentation Compteur
  //   contents of rom_1 (hex, n*v repeats v):
  //   42200003
  //   JMPZ
  //   JMPNZ
  //   JMPN
  //   JMPPZ
  //   Instruction
  //   2.Activation UAL
  //   Mémoire Données
  //   contents of rom_2 (hex, n*v repeats v):
  //   6 3 7 4
  //   3.Ecriture Registres
  //   Code opératoire
  //   DATA ou Adresse
  //   MUX0
  //   ALU
  //   Registre_A
  //   Registre_B
  //   MUX2
  //   MUX1
  //   Registre_C
endmodule

module c_MUX (
  input  Control,
  input  [15:0] Input_0,
  input  [15:0] Input_1,
  output [15:0] Output
);

  Multiplexer #(.width(16), .enable("false")) multiplexer_1 (.in0(Input_0), .in1(Input_1), .out(Output), .sel(Control));
endmodule

module c_Cycle (
  input  \Entrée_Horloge ,
  output Etat_1,
  output Etat_2,
  output Etat_3,
  output Etat_4
);

  wire d_ff_1_q, d_ff_1_qn, d_ff_2_q, d_ff_2_qn, not_1_out;

  D_Flip_Flop d_ff_1 (.clk(\Entrée_Horloge ), .D(d_ff_1_qn), .Q(d_ff_1_q), .Qn(d_ff_1_qn));  // open: preset, en, reset
  not not_1 (not_1_out, \Entrée_Horloge );
  D_Flip_Flop d_ff_2 (.clk(not_1_out), .D(d_ff_2_qn), .Q(d_ff_2_q), .Qn(d_ff_2_qn));  // open: preset, en, reset
  and and_1 (Etat_1, ~d_ff_1_q, ~d_ff_2_q);  // AND_Gate
  and and_2 (Etat_2, d_ff_1_q, ~d_ff_2_q);  // AND_Gate
  and and_3 (Etat_3, d_ff_1_q, d_ff_2_q);
  and and_4 (Etat_4, ~d_ff_1_q, d_ff_2_q);  // AND_Gate
endmodule

module c_ALU_16_bits (
  input  [15:0] Input_1,
  input  [15:0] Input_0,
  input  C3,
  input  C2,
  input  C1,
  input  C0,
  input  Enable,
  output [15:0] Output,
  output Negative,
  output Zero,
  output Carry
);

  wire adder_1_cout, adder_2_cout, and_2_out, and_3_out, and_4_out, and_5_out, and_6_out, and_7_out,
       and_8_out, and_9_out, and_10_out, and_11_out, and_12_out, bitfinder_1_found, bitfinder_2_found,
       comparator_1_eq, comparator_1_lt, comparator_2_lt, decoder_1_out0, decoder_1_out3, decoder_1_out4,
       decoder_1_out5, decoder_1_out6, decoder_1_out7, decoder_1_out8, decoder_1_out10, or_2_out, or_3_out,
       or_4_out, subtractor_1_bout, subtractor_2_bout, subtractor_3_bout;
  wire [15:0] adder_1_out, adder_2_out, and_1_out, divider_1_out, multiplexer_1_out, multiplier_1_cout,
       multiplier_1_out, not_1_out, not_2_out, or_1_out, subtractor_1_out, subtractor_2_out,
       subtractor_3_out, xor_1_out;

  assign not_1_out = ~Input_0;  // NOT_Gate not_1, 16 bits wide
  assign not_2_out = ~Input_1;  // NOT_Gate not_2, 16 bits wide
  assign and_1_out = Input_0 & Input_1;  // AND_Gate and_1, 16 bits wide
  assign or_1_out = Input_0 | Input_1;  // OR_Gate or_1, 16 bits wide
  Adder #(.width(16)) adder_1 (.a(Input_1), .b(16'h1), .out(adder_1_out), .cout(adder_1_cout));  // open: cin
  Subtractor #(.width(16)) subtractor_1 (
    .a(Input_1), .b(16'h1), .out(subtractor_1_out), .bout(subtractor_1_bout));  // open: bin
  Adder #(.width(16)) adder_2 (.a(Input_1), .b(Input_0), .out(adder_2_out), .cout(adder_2_cout));  // open: cin
  Subtractor #(.width(16)) subtractor_2 (
    .a(Input_0), .b(Input_1), .out(subtractor_2_out), .bout(subtractor_2_bout));  // open: bin
  Subtractor #(.width(16)) subtractor_3 (
    .a(Input_1), .b(Input_0), .out(subtractor_3_out), .bout(subtractor_3_bout));  // open: bin
  Multiplier #(.width(16)) multiplier_1 (
    .a(Input_1), .b(Input_0), .out(multiplier_1_out), .cout(multiplier_1_cout));  // open: cin
  BitFinder #(.width(16)) bitfinder_1 (.in(multiplier_1_cout), .found(bitfinder_1_found));  // open: index
  Divider #(.width(16)) divider_1 (.a(Input_1), .b(Input_0), .out(divider_1_out));  // open: upper, rem
  Comparator #(.width(16)) comparator_1 (
    .a(Input_1), .b(Input_0), .eq(comparator_1_eq), .lt(comparator_1_lt));  // open: gt
  assign xor_1_out = Input_0 ^ Input_1;  // XOR_Gate xor_1, 16 bits wide
  Decoder #(.select(4)) decoder_1 (
    .out0(decoder_1_out0), .out3(decoder_1_out3), .out4(decoder_1_out4), .out5(decoder_1_out5),
    .out6(decoder_1_out6), .out7(decoder_1_out7), .out8(decoder_1_out8), .out10(decoder_1_out10),
    .sel({C3, C2, C1, C0}));  // open: out1, out2, out9, out11, out12, out13, out14, out15, en
  and and_2 (and_2_out, comparator_1_lt, decoder_1_out10);
  Multiplexer #(.select(4), .width(16)) multiplexer_1 (
    .in0({16{1'b0}}), .in1(Input_0), .in2(Input_1), .in3(adder_1_out), .in4(subtractor_1_out),
    .in5(adder_2_out), .in6(subtractor_2_out), .in7(subtractor_3_out), .in8(multiplier_1_out),
    .in9(divider_1_out), .in10(Output), .in11(not_1_out), .in12(not_2_out), .in13(and_1_out),
    .in14(or_1_out), .in15(xor_1_out), .out(multiplexer_1_out), .sel({C3, C2, C1, C0}));  // open: en
  and and_3 (and_3_out, comparator_1_eq, decoder_1_out10);
  and and_4 (and_4_out, decoder_1_out8, bitfinder_1_found);
  and and_5 (and_5_out, decoder_1_out7, subtractor_3_bout);
  and and_6 (and_6_out, decoder_1_out6, subtractor_2_bout);
  and and_7 (and_7_out, decoder_1_out5, adder_2_cout);
  and and_8 (and_8_out, decoder_1_out4, subtractor_1_bout);
  and and_9 (and_9_out, decoder_1_out3, adder_1_cout);
  // Probe on multiplexer_1_out
  Comparator #(.width(16)) comparator_2 (.a(multiplexer_1_out), .b({16{1'b0}}), .lt(comparator_2_lt));  // open: gt, eq
  BitFinder #(.width(16)) bitfinder_2 (.in(multiplexer_1_out), .found(bitfinder_2_found));  // open: index
  and and_10 (and_10_out, ~decoder_1_out0, Enable);  // AND_Gate
  and and_11 (and_11_out, comparator_2_lt, ~decoder_1_out10);  // AND_Gate
  and and_12 (and_12_out, ~bitfinder_2_found, ~decoder_1_out10);  // AND_Gate
  or or_2 (or_2_out, and_4_out, and_5_out, and_6_out, and_7_out, and_8_out, and_9_out);
  Register #(.width(16)) register_1 (.D(multiplexer_1_out), .Q(Output), .clk(and_10_out));  // open: en, clr
  or or_3 (or_3_out, and_2_out, and_11_out);
  or or_4 (or_4_out, and_12_out, and_3_out);
  Register #(.width(1)) register_2 (.D(or_3_out), .Q(Negative), .clk(and_10_out));  // open: en, clr
  Register #(.width(1)) register_3 (.D(or_4_out), .Q(Zero), .clk(and_10_out));  // open: en, clr
  Register #(.width(1)) register_4 (.D(or_2_out), .Q(Carry), .clk(and_10_out));  // open: en, clr

  // Notes on the sheet:
  //   0001 : I0
  //   0010 : I1
  //   0011 : I1+1
  //   0100 : I1-1
  //   0101 : I0+I1
  //   0110 : I0-I1
  //   0111 : I1-I0
  //   1000 : I0*I1
  //   1001 : I1/I0
  //   1011 : NOT I0
  //   1100 : NOT I1
  //   1101:I0 AND I1
  //   1110:I0 OR I1
  //   1111:I0 XOR I1
  //   1010 : I1 CMP I0
  //   0000 : NOP
  //   1010 : I1 CMP I0
  //   Pour ne pas changer le resultat en sortie de l'UAL ni les indicateurs en cas de NOP
  //   Pour ne pas changer le resultat en sortie de l'UAL en cas de CMP
endmodule

module c_Compteur_16bits (
  input  [15:0] Input,
  input  Control,
  input  Reset,
  output [15:0] Output
);

  wire not_1_out;

  not not_1 (not_1_out, Reset);
  Counter #(.width(16), .max('hffff)) counter_1 (
    .load(Reset), .D(Input), .count(not_1_out), .Q(Output), .clk(Control));  // open: carry, clr
endmodule
